// Logisim project 1.circ as structural Verilog: 8 circuits, main circuit ALU
module ALU (
  input  [31:0] X,
  input  [31:0] Y,
  input  [3:0] AluOP,
  output Signed_Overflow,
  output UnSigned_Overflow,
  output Equal,
  output [31:0] Result,
  output [31:0] Result_2
);

  wire and_2_out, and_3_out, and_4_out, and_5_out, comparator_1_lt, comparator_2_lt, n32bitadder_1_c,
       not_2_out, not_3_out, not_4_out, not_6_out, not_7_out, or_2_out, or_3_out;
  wire [31:0] and_1_out, bit_extender_1_out, bit_extender_2_out, divider_1_out, multiplexer_1_out,
       multiplier_1_out, n32bitadder_1_out_5, not_1_out, not_5_out, or_1_out, remainder, shifter_1_out,
       shifter_2_out, shifter_3_out, timesHigh, xor_1_out;

  // Probe on X
  // Probe on X
  // Probe on Y
  // Probe on Y
  assign not_1_out = ~Y;  // NOT_Gate not_1, 32 bits wide
  not not_2 (not_2_out, AluOP[0]);
  // Probe on AluOP
  Multiplexer #(.width(32), .enable("false")) multiplexer_1 (
    .in0(not_1_out), .in1(Y), .out(multiplexer_1_out), .sel(AluOP[0]));
  not not_3 (not_3_out, Y[31]);
  not not_4 (not_4_out, X[31]);
  // Probe on Result
  // Probe on Result
  // Probe on Result_2
  Shifter #(.width(32)) shifter_1 (.in(X), .\dist (Y[4:0]), .out(shifter_1_out));
  Shifter #(.width(32), .shift("ar")) shifter_2 (.in(X), .\dist (Y[4:0]), .out(shifter_2_out));
  Shifter #(.width(32), .shift("lr")) shifter_3 (.in(X), .\dist (Y[4:0]), .out(shifter_3_out));
  Multiplier #(.width(32)) multiplier_1 (.a(X), .b(Y), .out(multiplier_1_out), .cin({32{1'b0}}), .cout(timesHigh));
  Divider #(.width(32)) divider_1 (.a(X), .b(Y), .out(divider_1_out), .rem(remainder));  // open: upper
  _32bitadder u_32bitadder_1 (
    .C(n32bitadder_1_c), .out_5(n32bitadder_1_out_5), .A(X), .B(multiplexer_1_out), .C0(not_2_out));
  assign and_1_out = X & Y;  // AND_Gate and_1, 32 bits wide
  assign or_1_out = X | Y;  // OR_Gate or_1, 32 bits wide
  assign xor_1_out = X ^ Y;  // XOR_Gate xor_1, 32 bits wide
  assign not_5_out = ~or_1_out;  // NOT_Gate not_5, 32 bits wide
  Comparator #(.width(32)) comparator_1 (.a(X), .b(Y), .lt(comparator_1_lt));  // open: gt, eq
  Comparator #(.width(32), .mode("unsigned")) comparator_2 (
    .a(X), .b(Y), .eq(Equal), .lt(comparator_2_lt));  // open: gt
  assign bit_extender_1_out = {{31{1'b0}}, comparator_1_lt};  // Bit_Extender bit_extender_1
  assign bit_extender_2_out = {{31{1'b0}}, comparator_2_lt};  // Bit_Extender bit_extender_2
  not not_6 (not_6_out, n32bitadder_1_out_5[31]);
  not not_7 (not_7_out, n32bitadder_1_c);
  Multiplexer #(.select(4), .width(32), .enable("false")) multiplexer_2 (
    .in0(shifter_1_out), .in1(shifter_2_out), .in2(shifter_3_out), .in3(multiplier_1_out),
    .in4(divider_1_out), .in5(n32bitadder_1_out_5), .in6(n32bitadder_1_out_5), .in7(and_1_out),
    .in8(or_1_out), .in9(xor_1_out), .in10(not_5_out), .in11(bit_extender_1_out), .in12(bit_extender_2_out),
    .in13({32{1'b0}}), .in14({32{1'b0}}), .in15({32{1'b0}}), .out(Result), .sel(AluOP));
  Multiplexer #(.select(4), .width(32), .enable("false")) multiplexer_3 (
    .in0({32{1'b0}}), .in1({32{1'b0}}), .in2({32{1'b0}}), .in3(timesHigh), .in4(remainder), .in5({32{1'b0}}),
    .in6({32{1'b0}}), .in7({32{1'b0}}), .in8({32{1'b0}}), .in9({32{1'b0}}), .in10({32{1'b0}}),
    .in11({32{1'b0}}), .in12({32{1'b0}}), .in13({32{1'b0}}), .in14({32{1'b0}}), .in15({32{1'b0}}),
    .out(Result_2), .sel(AluOP));
  and and_2 (and_2_out, not_3_out, not_4_out, n32bitadder_1_out_5[31]);
  and and_3 (and_3_out, not_6_out, Y[31], X[31]);
  and and_4 (and_4_out, Y[31], not_4_out, n32bitadder_1_out_5[31]);
  and and_5 (and_5_out, not_3_out, X[31], not_6_out);
  or or_2 (or_2_out, and_2_out, and_3_out);
  or or_3 (or_3_out, and_4_out, and_5_out);
  Multiplexer #(.select(4), .enable("false")) multiplexer_4 (
    .in0(1'b0), .in1(1'b0), .in2(1'b0), .in3(1'b0), .in4(1'b0), .in5(or_2_out), .in6(or_3_out), .in7(1'b0),
    .in8(1'b0), .in9(1'b0), .in10(1'b0), .in11(1'b0), .in12(1'b0), .in13(1'b0), .in14(1'b0), .in15(1'b0),
    .out(Signed_Overflow), .sel(AluOP));
  Multiplexer #(.select(4), .enable("false")) multiplexer_5 (
    .in0(1'b0), .in1(1'b0), .in2(1'b0), .in3(1'b0), .in4(1'b0), .in5(n32bitadder_1_c), .in6(not_7_out),
    .in7(1'b0), .in8(1'b0), .in9(1'b0), .in10(1'b0), .in11(1'b0), .in12(1'b0), .in13(1'b0), .in14(1'b0),
    .in15(1'b0), .out(UnSigned_Overflow), .sel(AluOP));

  // Other names for the same wires on the sheet: OF = Signed_Overflow; Result2[31:0] = Result_2; S[3:0] = AluOP;
  //   UOF = UnSigned_Overflow

  // Notes on the sheet:
  //   不要改变此引脚区域内容，也不要改变ALU封装形式
  //   输入引脚
  //   请在下方利用上方输入输出引脚的隧道信号构建ALU电路，ctrl+d复制选择部件
  //   华中科技大学计算机学院 计算机组成原理，鸣谢加州大学伯克利CS61C课程
  //   输出引脚
  //   探测区域
endmodule

module \演示电路  (
  input  [31:0] X,
  input  [31:0] Y,
  input  [3:0] ALUOP,
  output Signed_Overflow,
  output Unsigned_overflow,
  output [31:0] Result,
  output [31:0] Result_2,
  output Equal
);

  // Probe on X
  // Probe on X
  ALU alu_1 (
    .AluOP(ALUOP), .X(X), .Equal(Equal), .Result(Result), .Signed_Overflow(Signed_Overflow), .Y(Y),
    .Result_2(Result_2), .UnSigned_Overflow(Unsigned_overflow));
  // Probe on ALUOP
  // Probe on Y
  // Probe on Y
  // Probe on Result
  // Probe on Result
  // Probe on Result_2

  // Notes on the sheet:
  //   ALu电路无需调整位置即可连接在该电路中，并且不能出现蓝色线缆和三态输出
endmodule

module \等差数列  (
  input  [31:0] \数列初始值 ,
  input  [31:0] \等差值 ,
  input  \时钟 ,
  output [31:0] Result
);

  // Probe on \数列初始值 
  // Probe on \数列初始值 
  // Probe on \等差值 
  // Probe on \等差值 
  // Probe on Result
  // Probe on Result

  // Other names for the same wires on the sheet: 数列初值[31:0] = \数列初始值 ; 累加和[31:0] = Result

  // Notes on the sheet:
  //   不要改变此引脚区域内容，也不要改变ALU封装形式
  //   请在下方利用上方输入输出引脚的隧道信号构建等差数列求和电路，ctrl+d复制选择部件
  //   华中科技大学计算机学院 计算机组成原理，鸣谢加州大学伯克利CS61C课程
  //   输出引脚
  //   探测区域
endmodule

// 4bit\nadder
module _4bitadder (
  input  [3:0] B,
  input  C0,
  input  [3:0] A,
  output [3:0] S,
  output P,
  output G
);

  wire [3:0] carry_1_c, G1_out, P1_out;

  or P4 (P1_out[3], A[3], B[3]);
  or P3 (P1_out[2], A[2], B[2]);
  adder adder_1 (.S(S[3]), .A(A[3]), .B(B[3]), .C0(carry_1_c[2]));
  or P2 (P1_out[1], A[1], B[1]);
  adder adder_2 (.S(S[2]), .A(A[2]), .B(B[2]), .C0(carry_1_c[1]));
  or P1 (P1_out[0], A[0], B[0]);
  and G4 (G1_out[3], B[3], A[3]);
  adder adder_3 (.S(S[1]), .A(A[1]), .B(B[1]), .C0(carry_1_c[0]));
  and G3 (G1_out[2], B[2], A[2]);
  adder adder_4 (.S(S[0]), .A(A[0]), .B(B[0]), .C0(C0));
  and G2 (G1_out[1], A[1], B[1]);
  carry carry_1 (.P(P1_out), .G(G1_out), .P_2(P), .G_2(G), .C(carry_1_c), .C0(C0));
  and G1 (G1_out[0], A[0], B[0]);
endmodule

// 16bit\nadder
module _16bitadder (
  input  C0,
  input  [15:0] A,
  input  [15:0] B,
  output P,
  output G,
  output [15:0] S
);

  wire [3:0] carry_1_c, n4bitadder_4_g, n4bitadder_4_p;

  _4bitadder u_4bitadder_1 (
    .P(n4bitadder_4_p[3]), .G(n4bitadder_4_g[3]), .S(S[15:12]), .A(A[15:12]), .B(B[15:12]), .C0(carry_1_c[2]));
  carry carry_1 (.P(n4bitadder_4_p), .G(n4bitadder_4_g), .P_2(P), .G_2(G), .C(carry_1_c), .C0(C0));
  _4bitadder u_4bitadder_2 (
    .P(n4bitadder_4_p[2]), .G(n4bitadder_4_g[2]), .S(S[11:8]), .A(A[11:8]), .B(B[11:8]), .C0(carry_1_c[1]));
  _4bitadder u_4bitadder_3 (
    .P(n4bitadder_4_p[1]), .G(n4bitadder_4_g[1]), .S(S[7:4]), .A(A[7:4]), .B(B[7:4]), .C0(carry_1_c[0]));
  _4bitadder u_4bitadder_4 (.P(n4bitadder_4_p[0]), .G(n4bitadder_4_g[0]), .S(S[3:0]), .A(A[3:0]), .B(B[3:0]), .C0(C0));
endmodule

module adder (
  input  A,
  input  B,
  input  C0,
  output S
);

  xor xor_1 (S, A, B, C0);
endmodule

module carry (
  input  C0,
  input  [3:0] P,
  input  [3:0] G,
  output P_2,
  output G_2,
  output [3:0] C
);

  wire and_2_out, and_3_out, and_4_out, and_5_out, and_6_out, and_7_out, and_8_out, and_9_out, and_10_out,
       and_11_out, and_12_out, and_13_out, and_14_out;

  and and_1 (P_2, P[3], P[2], P[1], P[0]);
  and and_2 (and_2_out, P[3], P[2], P[1], G[0]);
  or or_1 (G_2, and_2_out, and_3_out, and_4_out, G[3]);
  and and_3 (and_3_out, P[3], P[2], G[1]);
  and and_4 (and_4_out, P[3], G[2]);
  and and_5 (and_5_out, P[3], P[2], P[1], P[0], C0);
  and and_6 (and_6_out, P[3], P[2], P[1], G[0]);
  and and_7 (and_7_out, P[3], P[2], G[1]);
  or C4 (C[3], and_5_out, and_6_out, and_7_out, and_8_out, G[3]);
  and and_8 (and_8_out, P[3], G[2]);
  or C3 (C[2], and_10_out, and_9_out, and_11_out, G[2]);
  and and_9 (and_9_out, P[2], P[1], G[0]);
  and and_10 (and_10_out, P[2], G[1]);
  and and_11 (and_11_out, P[2], P[1], P[0], C0);
  and and_12 (and_12_out, G[0], P[1]);
  or C2 (C[1], and_12_out, and_13_out, G[1]);
  and and_13 (and_13_out, P[0], P[1], C0);
  or C1 (C[0], G[0], and_14_out);
  and and_14 (and_14_out, P[0], C0);
endmodule

// 32bit\nadder
module _32bitadder (
  input  [31:0] A,
  input  [31:0] B,
  input  C0,
  output C,
  output [31:0] out_5
);

  wire [1:0] n16bitadder_2_g, n16bitadder_2_p;
  wire [3:0] carry_1_c;

  _16bitadder u_16bitadder_1 (
    .P(n16bitadder_2_p[1]), .G(n16bitadder_2_g[1]), .S(out_5[31:16]), .A(A[31:16]), .B(B[31:16]),
    .C0(carry_1_c[0]));
  carry carry_1 (
    .P({2'b00, n16bitadder_2_p}), .G({2'b00, n16bitadder_2_g}), .C({carry_1_c[3:2], C, carry_1_c[0]}), .C0(C0));  // open: P_2, G_2
  _16bitadder u_16bitadder_2 (
    .P(n16bitadder_2_p[0]), .G(n16bitadder_2_g[0]), .S(out_5[15:0]), .A(A[15:0]), .B(B[15:0]), .C0(C0));
endmodule
