// Logisim project 2.circ as structural Verilog: 4 circuits, main circuit main
module main (
  input  [4:0] Reg1_num,
  input  [4:0] Reg2,
  input  [4:0] Write_Reg_num,
  input  [31:0] Din,
  input  Write_Enable,
  input  Clock,
  output [31:0] Reg1,
  output [31:0] s0_Value,
  output [31:0] s1_Value,
  output [31:0] s2_Value,
  output [31:0] ra_Value,
  output [31:0] Reg2_2
);


  // Other names for the same wires on the sheet: clk = Clock; ra[31:0] = ra_Value; reg2_num[4:0] = Reg2;
  //   reg2_t[31:0] = Reg2_2; s0[31:0] = s0_Value; s1[31:0] = s1_Value; s2[31:0] = s2_Value; WE = Write_Enable;
  //   write_data[31:0] = Din

  // Notes on the sheet:
  //   输入引脚
  //   输出引脚
  //   Debug引脚，便于观测寄存器值
  //   请勿修改引脚以及封装，直接使用隧道连接电路
endmodule

module test (
);

  wire undriven;

  main main_1 (.Clock(undriven));  // open: Reg1_num, Reg2, Write_Reg_num, Din, Write_Enable, Reg1, Reg2_2, s0_Value, s1_Value, s2_Value, ra_Value
endmodule

module mips (
  input  [31:0] Din,
  input  WE,
  input  CLK,
  input  [4:0] R1_num,
  input  [4:0] R2_num,
  input  [4:0] W_num
);

  wire decoder_1_out0, decoder_1_out1, decoder_1_out2, decoder_1_out3, decoder_2_out0, decoder_2_out1,
       decoder_2_out2, decoder_2_out3, decoder_2_out4, decoder_2_out5, decoder_2_out6, decoder_2_out7;

  Decoder #(.select(2), .enable("false")) decoder_1 (
    .out0(decoder_1_out0), .out1(decoder_1_out1), .out2(decoder_1_out2), .out3(decoder_1_out3),
    .sel(R1_num[4:3]));
  Decoder #(.select(3), .enable("false")) decoder_2 (
    .out0(decoder_2_out0), .out1(decoder_2_out1), .out2(decoder_2_out2), .out3(decoder_2_out3),
    .out4(decoder_2_out4), .out5(decoder_2_out5), .out6(decoder_2_out6), .out7(decoder_2_out7),
    .sel(R1_num[2:0]));
  \reg  reg_1 (
    .raw1(decoder_1_out0), .column1(decoder_2_out0));  // open: r1Out, r2Out, directOut, raw2, column2, writeRaw, writeColumn, WE, CLK, reset, inData
  \reg  reg_2 (
    .raw1(decoder_1_out1), .column1(decoder_2_out0));  // open: r1Out, r2Out, directOut, raw2, column2, writeRaw, writeColumn, WE, CLK, reset, inData
  \reg  reg_3 (
    .raw1(decoder_1_out2), .column1(decoder_2_out0));  // open: r1Out, r2Out, directOut, raw2, column2, writeRaw, writeColumn, WE, CLK, reset, inData
  \reg  reg_4 (
    .raw1(decoder_1_out3), .column1(decoder_2_out0));  // open: r1Out, r2Out, directOut, raw2, column2, writeRaw, writeColumn, WE, CLK, reset, inData
  Decoder #(.select(2), .enable("false")) decoder_3 (.sel(R2_num[4:3]));  // open: out0, out1, out2, out3
  Decoder #(.select(3), .enable("false")) decoder_4 (.sel(R2_num[2:0]));  // open: out0, out1, out2, out3, out4, out5, out6, out7
  \reg  reg_5 (
    .raw1(decoder_1_out0), .column1(decoder_2_out1));  // open: r1Out, r2Out, directOut, raw2, column2, writeRaw, writeColumn, WE, CLK, reset, inData
  \reg  reg_6 (
    .raw1(decoder_1_out1), .column1(decoder_2_out1));  // open: r1Out, r2Out, directOut, raw2, column2, writeRaw, writeColumn, WE, CLK, reset, inData
  \reg  reg_7 (
    .raw1(decoder_1_out2), .column1(decoder_2_out1));  // open: r1Out, r2Out, directOut, raw2, column2, writeRaw, writeColumn, WE, CLK, reset, inData
  \reg  reg_8 (
    .raw1(decoder_1_out3), .column1(decoder_2_out1));  // open: r1Out, r2Out, directOut, raw2, column2, writeRaw, writeColumn, WE, CLK, reset, inData
  Decoder #(.select(2), .enable("false")) decoder_5 (.sel(W_num[4:3]));  // open: out0, out1, out2, out3
  Decoder #(.select(3), .enable("false")) decoder_6 (.sel(W_num[2:0]));  // open: out0, out1, out2, out3, out4, out5, out6, out7
  \reg  reg_9 (
    .raw1(decoder_1_out0), .column1(decoder_2_out2));  // open: r1Out, r2Out, directOut, raw2, column2, writeRaw, writeColumn, WE, CLK, reset, inData
  \reg  reg_10 (
    .raw1(decoder_1_out1), .column1(decoder_2_out2));  // open: r1Out, r2Out, directOut, raw2, column2, writeRaw, writeColumn, WE, CLK, reset, inData
  \reg  reg_11 (
    .raw1(decoder_1_out2), .column1(decoder_2_out2));  // open: r1Out, r2Out, directOut, raw2, column2, writeRaw, writeColumn, WE, CLK, reset, inData
  \reg  reg_12 (
    .raw1(decoder_1_out3), .column1(decoder_2_out2));  // open: r1Out, r2Out, directOut, raw2, column2, writeRaw, writeColumn, WE, CLK, reset, inData
  \reg  reg_13 (
    .raw1(decoder_1_out0), .column1(decoder_2_out3));  // open: r1Out, r2Out, directOut, raw2, column2, writeRaw, writeColumn, WE, CLK, reset, inData
  \reg  reg_14 (
    .raw1(decoder_1_out1), .column1(decoder_2_out3));  // open: r1Out, r2Out, directOut, raw2, column2, writeRaw, writeColumn, WE, CLK, reset, inData
  \reg  reg_15 (
    .raw1(decoder_1_out2), .column1(decoder_2_out3));  // open: r1Out, r2Out, directOut, raw2, column2, writeRaw, writeColumn, WE, CLK, reset, inData
  \reg  reg_16 (
    .raw1(decoder_1_out3), .column1(decoder_2_out3));  // open: r1Out, r2Out, directOut, raw2, column2, writeRaw, writeColumn, WE, CLK, reset, inData
  \reg  reg_17 (
    .raw1(decoder_1_out0), .column1(decoder_2_out4));  // open: r1Out, r2Out, directOut, raw2, column2, writeRaw, writeColumn, WE, CLK, reset, inData
  \reg  reg_18 (
    .raw1(decoder_1_out1), .column1(decoder_2_out4));  // open: r1Out, r2Out, directOut, raw2, column2, writeRaw, writeColumn, WE, CLK, reset, inData
  \reg  reg_19 (
    .raw1(decoder_1_out2), .column1(decoder_2_out4));  // open: r1Out, r2Out, directOut, raw2, column2, writeRaw, writeColumn, WE, CLK, reset, inData
  \reg  reg_20 (
    .raw1(decoder_1_out3), .column1(decoder_2_out4));  // open: r1Out, r2Out, directOut, raw2, column2, writeRaw, writeColumn, WE, CLK, reset, inData
  \reg  reg_21 (
    .raw1(decoder_1_out0), .column1(decoder_2_out5));  // open: r1Out, r2Out, directOut, raw2, column2, writeRaw, writeColumn, WE, CLK, reset, inData
  \reg  reg_22 (
    .raw1(decoder_1_out1), .column1(decoder_2_out5));  // open: r1Out, r2Out, directOut, raw2, column2, writeRaw, writeColumn, WE, CLK, reset, inData
  \reg  reg_23 (
    .raw1(decoder_1_out2), .column1(decoder_2_out5));  // open: r1Out, r2Out, directOut, raw2, column2, writeRaw, writeColumn, WE, CLK, reset, inData
  \reg  reg_24 (
    .raw1(decoder_1_out3), .column1(decoder_2_out5));  // open: r1Out, r2Out, directOut, raw2, column2, writeRaw, writeColumn, WE, CLK, reset, inData
  \reg  reg_25 (
    .raw1(decoder_1_out0), .column1(decoder_2_out6));  // open: r1Out, r2Out, directOut, raw2, column2, writeRaw, writeColumn, WE, CLK, reset, inData
  \reg  reg_26 (
    .raw1(decoder_1_out1), .column1(decoder_2_out6));  // open: r1Out, r2Out, directOut, raw2, column2, writeRaw, writeColumn, WE, CLK, reset, inData
  \reg  reg_27 (
    .raw1(decoder_1_out2), .column1(decoder_2_out6));  // open: r1Out, r2Out, directOut, raw2, column2, writeRaw, writeColumn, WE, CLK, reset, inData
  \reg  reg_28 (
    .raw1(decoder_1_out3), .column1(decoder_2_out6));  // open: r1Out, r2Out, directOut, raw2, column2, writeRaw, writeColumn, WE, CLK, reset, inData
  \reg  reg_29 (
    .raw1(decoder_1_out0), .column1(decoder_2_out7));  // open: r1Out, r2Out, directOut, raw2, column2, writeRaw, writeColumn, WE, CLK, reset, inData
  \reg  reg_30 (
    .raw1(decoder_1_out1), .column1(decoder_2_out7));  // open: r1Out, r2Out, directOut, raw2, column2, writeRaw, writeColumn, WE, CLK, reset, inData
  \reg  reg_31 (
    .raw1(decoder_1_out2), .column1(decoder_2_out7));  // open: r1Out, r2Out, directOut, raw2, column2, writeRaw, writeColumn, WE, CLK, reset, inData
  \reg  reg_32 (
    .raw1(decoder_1_out3), .column1(decoder_2_out7));  // open: r1Out, r2Out, directOut, raw2, column2, writeRaw, writeColumn, WE, CLK, reset, inData
endmodule

module \reg  (
  input  [31:0] inData,
  input  raw1,
  input  column1,
  input  raw2,
  input  column2,
  input  writeRaw,
  input  writeColumn,
  input  WE,
  input  CLK,
  input  reset,
  output [31:0] r1Out,
  output [31:0] r2Out,
  output [31:0] directOut
);

  wire and_1_out, and_2_out, and_3_out, canRead_out;

  assign r1Out = and_1_out ? directOut : 32'bz;  // Controlled_Buffer r1
  and and_1 (and_1_out, raw1, column1, canRead_out);
  assign r2Out = and_2_out ? directOut : 32'bz;  // Controlled_Buffer r2
  and and_2 (and_2_out, raw2, column2, canRead_out);
  nand canRead (canRead_out, CLK, WE);
  and and_3 (and_3_out, writeRaw, writeColumn, WE);
  Register #(.width(32)) register_1 (.D(inData), .en(and_3_out), .Q(directOut), .clk(CLK), .clr(reset));
endmodule
