// Logisim project 2m.circ as structural Verilog: 3 circuits, main circuit main
module main (
  input  [4:0] Reg1_num,
  input  [4:0] Reg2,
  input  [4:0] Write_Reg_num,
  input  [31:0] Din,
  input  Write_Enable,
  input  Clock,
  output [31:0] Reg1,
  output [31:0] s0_Value,
  output [31:0] s1_Value,
  output [31:0] s2_Value,
  output [31:0] ra_Value,
  output [31:0] Reg2_2
);

  wire and_1_out, and_2_out, and_3_out, and_4_out, and_5_out, and_6_out, and_7_out, and_8_out, and_9_out,
       and_10_out, and_11_out, and_12_out, and_13_out, and_14_out, and_15_out, and_16_out, and_17_out,
       and_18_out, and_19_out, and_20_out, and_21_out, and_22_out, and_23_out, and_24_out, and_25_out,
       and_26_out, and_27_out, and_28_out, and_29_out, and_30_out, and_31_out, decoder_1_out1,
       decoder_1_out2, decoder_1_out3, decoder_1_out4, decoder_1_out5, decoder_1_out6, decoder_1_out7,
       decoder_2_out0, decoder_2_out1, decoder_2_out2, decoder_2_out3, decoder_2_out4, decoder_2_out5,
       decoder_2_out6, decoder_2_out7, decoder_3_out0, decoder_3_out1, decoder_3_out2, decoder_3_out3,
       decoder_4_out0, decoder_4_out1, decoder_4_out2, decoder_4_out3, decoder_4_out4, decoder_4_out5,
       decoder_4_out6, decoder_4_out7, decoder_5_out0, decoder_5_out1, decoder_5_out2, decoder_5_out3,
       decoder_5_out4, decoder_5_out5, decoder_5_out6, decoder_5_out7;
  wire [31:0] multiplexer_1_out, multiplexer_2_out, multiplexer_3_out, multiplexer_4_out, multiplexer_7_out,
       multiplexer_8_out, multiplexer_9_out, multiplexer_10_out, register_1_q, register_2_q, register_3_q,
       register_4_q, register_5_q, register_6_q, register_7_q, register_11_q, register_12_q, register_13_q,
       register_14_q, register_15_q, register_16_q, register_17_q, register_18_q, register_19_q,
       register_20_q, register_21_q, register_22_q, register_23_q, register_24_q, register_25_q,
       register_26_q, register_27_q, register_28_q, register_29_q, register_30_q;

  Decoder #(.select(3), .enable("false")) decoder_1 (
    .out1(decoder_1_out1), .out2(decoder_1_out2), .out3(decoder_1_out3), .out4(decoder_1_out4),
    .out5(decoder_1_out5), .out6(decoder_1_out6), .out7(decoder_1_out7), .sel(Write_Reg_num[2:0]));  // open: out0
  Decoder #(.select(3), .enable("false")) decoder_2 (
    .out0(decoder_2_out0), .out1(decoder_2_out1), .out2(decoder_2_out2), .out3(decoder_2_out3),
    .out4(decoder_2_out4), .out5(decoder_2_out5), .out6(decoder_2_out6), .out7(decoder_2_out7),
    .sel(Write_Reg_num[2:0]));
  Decoder #(.select(2), .enable("false")) decoder_3 (
    .out0(decoder_3_out0), .out1(decoder_3_out1), .out2(decoder_3_out2), .out3(decoder_3_out3),
    .sel(Write_Reg_num[4:3]));
  and and_1 (and_1_out, decoder_1_out1, Write_Enable, decoder_3_out0);
  and and_2 (and_2_out, decoder_1_out2, Write_Enable, decoder_3_out0);
  and and_3 (and_3_out, decoder_1_out3, Write_Enable, decoder_3_out0);
  and and_4 (and_4_out, decoder_1_out4, Write_Enable, decoder_3_out0);
  and and_5 (and_5_out, decoder_1_out5, Write_Enable, decoder_3_out0);
  and and_6 (and_6_out, decoder_1_out6, Write_Enable, decoder_3_out0);
  and and_7 (and_7_out, decoder_1_out7, Write_Enable, decoder_3_out0);
  and and_8 (and_8_out, decoder_2_out0, Write_Enable, decoder_3_out2);
  and and_9 (and_9_out, decoder_2_out1, Write_Enable, decoder_3_out2);
  and and_10 (and_10_out, decoder_2_out2, Write_Enable, decoder_3_out2);
  and and_11 (and_11_out, decoder_2_out3, Write_Enable, decoder_3_out2);
  and and_12 (and_12_out, decoder_2_out4, Write_Enable, decoder_3_out2);
  and and_13 (and_13_out, decoder_2_out5, Write_Enable, decoder_3_out2);
  and and_14 (and_14_out, decoder_2_out6, Write_Enable, decoder_3_out2);
  and and_15 (and_15_out, decoder_2_out7, Write_Enable, decoder_3_out2);
  Register #(.width(32)) register_1 (.D(Din), .en(and_1_out), .Q(register_1_q), .clk(Clock), .clr(1'b0));
  Register #(.width(32)) register_2 (.D(Din), .en(and_2_out), .Q(register_2_q), .clk(Clock), .clr(1'b0));
  Register #(.width(32)) register_3 (.D(Din), .en(and_3_out), .Q(register_3_q), .clk(Clock), .clr(1'b0));
  Register #(.width(32)) register_4 (.D(Din), .en(and_4_out), .Q(register_4_q), .clk(Clock), .clr(1'b0));
  Register #(.width(32)) register_5 (.D(Din), .en(and_5_out), .Q(register_5_q), .clk(Clock), .clr(1'b0));
  Register #(.width(32)) register_6 (.D(Din), .en(and_6_out), .Q(register_6_q), .clk(Clock), .clr(1'b0));
  Register #(.width(32)) register_7 (.D(Din), .en(and_7_out), .Q(register_7_q), .clk(Clock), .clr(1'b0));
  Register #(.width(32)) register_8 (.D(Din), .en(and_8_out), .Q(s0_Value), .clk(Clock), .clr(1'b0));
  Register #(.width(32)) register_9 (.D(Din), .en(and_9_out), .Q(s1_Value), .clk(Clock), .clr(1'b0));
  Register #(.width(32)) register_10 (.D(Din), .en(and_10_out), .Q(s2_Value), .clk(Clock), .clr(1'b0));
  Register #(.width(32)) register_11 (.D(Din), .en(and_11_out), .Q(register_11_q), .clk(Clock), .clr(1'b0));
  Register #(.width(32)) register_12 (.D(Din), .en(and_12_out), .Q(register_12_q), .clk(Clock), .clr(1'b0));
  Register #(.width(32)) register_13 (.D(Din), .en(and_13_out), .Q(register_13_q), .clk(Clock), .clr(1'b0));
  Register #(.width(32)) register_14 (.D(Din), .en(and_14_out), .Q(register_14_q), .clk(Clock), .clr(1'b0));
  Register #(.width(32)) register_15 (.D(Din), .en(and_15_out), .Q(register_15_q), .clk(Clock), .clr(1'b0));
  Multiplexer #(.select(3), .width(32), .enable("false")) multiplexer_1 (
    .in0({32{1'b0}}), .in1(register_1_q), .in2(register_2_q), .in3(register_3_q), .in4(register_4_q),
    .in5(register_5_q), .in6(register_6_q), .in7(register_7_q), .out(multiplexer_1_out), .sel(Reg1_num[2:0]));
  Multiplexer #(.select(3), .width(32), .enable("false")) multiplexer_2 (
    .in0({32{1'b0}}), .in1(register_1_q), .in2(register_2_q), .in3(register_3_q), .in4(register_4_q),
    .in5(register_5_q), .in6(register_6_q), .in7(register_7_q), .out(multiplexer_2_out), .sel(Reg2[2:0]));
  Multiplexer #(.select(3), .width(32), .enable("false")) multiplexer_3 (
    .in0(s0_Value), .in1(s1_Value), .in2(s2_Value), .in3(register_11_q), .in4(register_12_q),
    .in5(register_13_q), .in6(register_14_q), .in7(register_15_q), .out(multiplexer_3_out),
    .sel(Reg1_num[2:0]));
  Multiplexer #(.select(3), .width(32), .enable("false")) multiplexer_4 (
    .in0(s0_Value), .in1(s1_Value), .in2(s2_Value), .in3(register_11_q), .in4(register_12_q),
    .in5(register_13_q), .in6(register_14_q), .in7(register_15_q), .out(multiplexer_4_out), .sel(Reg2[2:0]));
  Multiplexer #(.select(2), .width(32), .enable("false")) multiplexer_5 (
    .in0(multiplexer_1_out), .in1(multiplexer_7_out), .in2(multiplexer_3_out), .in3(multiplexer_9_out),
    .out(Reg1), .sel(Reg1_num[4:3]));
  Decoder #(.select(3), .enable("false")) decoder_4 (
    .out0(decoder_4_out0), .out1(decoder_4_out1), .out2(decoder_4_out2), .out3(decoder_4_out3),
    .out4(decoder_4_out4), .out5(decoder_4_out5), .out6(decoder_4_out6), .out7(decoder_4_out7),
    .sel(Write_Reg_num[2:0]));
  Decoder #(.select(3), .enable("false")) decoder_5 (
    .out0(decoder_5_out0), .out1(decoder_5_out1), .out2(decoder_5_out2), .out3(decoder_5_out3),
    .out4(decoder_5_out4), .out5(decoder_5_out5), .out6(decoder_5_out6), .out7(decoder_5_out7),
    .sel(Write_Reg_num[2:0]));
  Multiplexer #(.select(2), .width(32), .enable("false")) multiplexer_6 (
    .in0(multiplexer_2_out), .in1(multiplexer_8_out), .in2(multiplexer_4_out), .in3(multiplexer_10_out),
    .out(Reg2_2), .sel(Reg2[4:3]));
  and and_16 (and_16_out, decoder_4_out0, Write_Enable, decoder_3_out1);
  and and_17 (and_17_out, decoder_4_out1, Write_Enable, decoder_3_out1);
  and and_18 (and_18_out, decoder_4_out2, Write_Enable, decoder_3_out1);
  and and_19 (and_19_out, decoder_4_out3, Write_Enable, decoder_3_out1);
  and and_20 (and_20_out, decoder_4_out4, Write_Enable, decoder_3_out1);
  and and_21 (and_21_out, decoder_4_out5, Write_Enable, decoder_3_out1);
  and and_22 (and_22_out, decoder_4_out6, Write_Enable, decoder_3_out1);
  and and_23 (and_23_out, decoder_4_out7, Write_Enable, decoder_3_out1);
  and and_24 (and_24_out, decoder_5_out0, Write_Enable, decoder_3_out3);
  and and_25 (and_25_out, decoder_5_out1, Write_Enable, decoder_3_out3);
  and and_26 (and_26_out, decoder_5_out2, Write_Enable, decoder_3_out3);
  and and_27 (and_27_out, decoder_5_out3, Write_Enable, decoder_3_out3);
  and and_28 (and_28_out, decoder_5_out4, Write_Enable, decoder_3_out3);
  and and_29 (and_29_out, decoder_5_out5, Write_Enable, decoder_3_out3);
  and and_30 (and_30_out, decoder_5_out6, Write_Enable, decoder_3_out3);
  and and_31 (and_31_out, decoder_5_out7, Write_Enable, decoder_3_out3);
  Register #(.width(32)) register_16 (.D(Din), .en(and_16_out), .Q(register_16_q), .clk(Clock), .clr(1'b0));
  Register #(.width(32)) register_17 (.D(Din), .en(and_17_out), .Q(register_17_q), .clk(Clock), .clr(1'b0));
  Register #(.width(32)) register_18 (.D(Din), .en(and_18_out), .Q(register_18_q), .clk(Clock), .clr(1'b0));
  Register #(.width(32)) register_19 (.D(Din), .en(and_19_out), .Q(register_19_q), .clk(Clock), .clr(1'b0));
  Register #(.width(32)) register_20 (.D(Din), .en(and_20_out), .Q(register_20_q), .clk(Clock), .clr(1'b0));
  Register #(.width(32)) register_21 (.D(Din), .en(and_21_out), .Q(register_21_q), .clk(Clock), .clr(1'b0));
  Register #(.width(32)) register_22 (.D(Din), .en(and_22_out), .Q(register_22_q), .clk(Clock), .clr(1'b0));
  Register #(.width(32)) register_23 (.D(Din), .en(and_23_out), .Q(register_23_q), .clk(Clock), .clr(1'b0));
  Register #(.width(32)) register_24 (.D(Din), .en(and_24_out), .Q(register_24_q), .clk(Clock), .clr(1'b0));
  Register #(.width(32)) register_25 (.D(Din), .en(and_25_out), .Q(register_25_q), .clk(Clock), .clr(1'b0));
  Register #(.width(32)) register_26 (.D(Din), .en(and_26_out), .Q(register_26_q), .clk(Clock), .clr(1'b0));
  Register #(.width(32)) register_27 (.D(Din), .en(and_27_out), .Q(register_27_q), .clk(Clock), .clr(1'b0));
  Register #(.width(32)) register_28 (.D(Din), .en(and_28_out), .Q(register_28_q), .clk(Clock), .clr(1'b0));
  Register #(.width(32)) register_29 (.D(Din), .en(and_29_out), .Q(register_29_q), .clk(Clock), .clr(1'b0));
  Register #(.width(32)) register_30 (.D(Din), .en(and_30_out), .Q(register_30_q), .clk(Clock), .clr(1'b0));
  Register #(.width(32)) register_31 (.D(Din), .en(and_31_out), .Q(ra_Value), .clk(Clock), .clr(1'b0));
  Multiplexer #(.select(3), .width(32), .enable("false")) multiplexer_7 (
    .in0(register_16_q), .in1(register_17_q), .in2(register_18_q), .in3(register_19_q), .in4(register_20_q),
    .in5(register_21_q), .in6(register_22_q), .in7(register_23_q), .out(multiplexer_7_out),
    .sel(Reg1_num[2:0]));
  Multiplexer #(.select(3), .width(32), .enable("false")) multiplexer_8 (
    .in0(register_16_q), .in1(register_17_q), .in2(register_18_q), .in3(register_19_q), .in4(register_20_q),
    .in5(register_21_q), .in6(register_22_q), .in7(register_23_q), .out(multiplexer_8_out), .sel(Reg2[2:0]));
  Multiplexer #(.select(3), .width(32), .enable("false")) multiplexer_9 (
    .in0(register_24_q), .in1(register_25_q), .in2(register_26_q), .in3(register_27_q), .in4(register_28_q),
    .in5(register_29_q), .in6(register_30_q), .in7(ra_Value), .out(multiplexer_9_out), .sel(Reg1_num[2:0]));
  Multiplexer #(.select(3), .width(32), .enable("false")) multiplexer_10 (
    .in0(register_24_q), .in1(register_25_q), .in2(register_26_q), .in3(register_27_q), .in4(register_28_q),
    .in5(register_29_q), .in6(register_30_q), .in7(ra_Value), .out(multiplexer_10_out), .sel(Reg2[2:0]));

  // Other names for the same wires on the sheet: clk = Clock; ra[31:0] = ra_Value; reg2_num[4:0] = Reg2;
  //   reg2_t[31:0] = Reg2_2; s0[31:0] = s0_Value; s1[31:0] = s1_Value; s2[31:0] = s2_Value; WE = Write_Enable;
  //   write_data[31:0] = Din

  // Notes on the sheet:
  //   输入引脚
  //   输出引脚
  //   Debug引脚，便于观测寄存器值
  //   请勿修改引脚以及封装，直接使用隧道连接电路
endmodule

module test (
);

  main main_1 ();  // open: Reg1_num, Reg2, Write_Reg_num, Din, Write_Enable, Clock, Reg1, Reg2_2, s0_Value, s1_Value, s2_Value, ra_Value
endmodule

module calc (
);

  wire alu_1_p5, clock_1_out, comparator_1_eq, comparator_2_eq, comparator_3_eq, comparator_4_eq,
       counter_2_q, counter_carry, multiplexer_1_out;
  wire [2:0] deliver_q;
  wire [3:0] main_1_reg1, main_1_reg1_2, main_1_reg1_3, main_1_reg1_4, main_1_reg1_5, main_1_reg1_6,
       main_1_reg1_7, main_1_reg1_8;
  wire [4:0] counter_q, writeAddr_q;
  wire [5:0] multiplexer_2_out;
  wire [31:0] alu_1_p4, ram_1_data;

  Multiplexer #(.enable("false")) multiplexer_1 (
    .in0(clock_1_out), .in1(1'b0), .out(multiplexer_1_out), .sel(counter_2_q));
  Clock clock_1 (.out(clock_1_out));
  Hex_Digit_Display hex_digit_display_1 (.value(main_1_reg1_8));  // open: dp
  Hex_Digit_Display hex_digit_display_2 (.value(main_1_reg1_7));  // open: dp
  Hex_Digit_Display hex_digit_display_3 (.value(main_1_reg1_6));  // open: dp
  Counter #(.width(3), .max('h5)) deliver (
    .load(1'b0), .count(1'b1), .Q(deliver_q), .clk(multiplexer_1_out));  // open: D, carry, clr
  Hex_Digit_Display hex_digit_display_4 (.value(main_1_reg1_5));  // open: dp
  Register #(.width(5)) writeAddr (.D(counter_q), .en(1'b1), .Q(writeAddr_q), .clk(comparator_4_eq));  // open: clr
  Hex_Digit_Display hex_digit_display_5 (.value(main_1_reg1_4));  // open: dp
  Counter #(.width(5), .max('h1f)) counter (
    .load(1'b0), .count(1'b1), .Q(counter_q), .carry(counter_carry), .clk(comparator_4_eq));  // open: D, clr
  Comparator #(.width(3), .mode("unsigned")) comparator_1 (
    .a(deliver_q), .b(3'b001), .eq(comparator_1_eq));  // open: gt, lt
  Comparator #(.width(3), .mode("unsigned")) comparator_2 (
    .a(deliver_q), .b(3'b010), .eq(comparator_2_eq));  // open: gt, lt
  Comparator #(.width(3), .mode("unsigned")) comparator_3 (
    .a(deliver_q), .b(3'b011), .eq(comparator_3_eq));  // open: gt, lt
  Comparator #(.width(3), .mode("unsigned")) comparator_4 (
    .a(deliver_q), .b(3'b100), .eq(comparator_4_eq));  // open: gt, lt
  Hex_Digit_Display hex_digit_display_6 (.value(main_1_reg1_3));  // open: dp
  Hex_Digit_Display hex_digit_display_7 (.value(main_1_reg1_2));  // open: dp
  Counter #(.width(1), .max('h1), .trigger("falling")) counter_2 (
    .load(1'b0), .count(1'b1), .Q(counter_2_q), .clk(counter_carry));  // open: D, carry, clr
  Hex_Digit_Display hex_digit_display_8 (.value(main_1_reg1));  // open: dp
  Multiplexer #(.width(6), .enable("false")) multiplexer_2 (
    .in0({1'b1, writeAddr_q}), .in1({1'b0, counter_q}), .out(multiplexer_2_out), .sel(comparator_1_eq));
  // Probe on {main_1_reg1_8, main_1_reg1_7, main_1_reg1_6, main_1_reg1_5, main_1_reg1_4, main_1_reg1_3, main_1_reg1_2, main_1_reg1}
  main main_1 (
    .Reg1_num(5'b00001), .Write_Reg_num(5'b00001), .Din(alu_1_p4), .Write_Enable(1'b1),
    .Clock(comparator_2_eq),
    .Reg1({main_1_reg1_8, main_1_reg1_7, main_1_reg1_6, main_1_reg1_5, main_1_reg1_4, main_1_reg1_3, main_1_reg1_2, main_1_reg1}));  // open: Reg2, Reg2_2, s0_Value, s1_Value, s2_Value, ra_Value
  // Probe on {main_1_reg1_8, main_1_reg1_7, main_1_reg1_6, main_1_reg1_5, main_1_reg1_4, main_1_reg1_3, main_1_reg1_2, main_1_reg1}
  RAM #(.addrWidth(6), .dataWidth(32), .bus("separate")) ram_1 (
    .addr(multiplexer_2_out),
    .din({main_1_reg1_8, main_1_reg1_7, main_1_reg1_6, main_1_reg1_5, main_1_reg1_4, main_1_reg1_3, main_1_reg1_2, main_1_reg1}),
    .data(ram_1_data), .str(comparator_3_eq), .clk(comparator_3_eq), .ld(1'b1));  // open: sel, clr
  // Probe on ram_1_data
  // Probe on alu_1_p5
  // ALU alu_1: pin names not known; wires that end beside it: {main_1_reg1_8, main_1_reg1_7, main_1_reg1_6, main_1_reg1_5, main_1_reg1_4, main_1_reg1_3, main_1_reg1_2, main_1_reg1}, ram_1_data, 4'b0101, alu_1_p4, alu_1_p5

  // Notes on the sheet:
  //   1取数据，2写寄存器，3写ram，4地址加1
endmodule
